# Fritzing sketch Biot_1.3 (saved by Fritzing 0.9.3b)
breadboards: 1

parts:
  DS1 = DS18B20 1-Wire Temperature Sensor [part_number=DS18B20]
  BMP280_Breakout1 = BMP280 Breakout Board [part_number=BMP280]
  LED1 = LED - 5mm [color="Red (633nm)" package="5 mm [THT]"]
  Componente1 = FC-28 Soil Hygrometer Module - Probe
  Componente2 = FC-28 Soil Hygrometer Module
  MQ-3_Sensor1 = MQ-3 Breakout Board
  Componente3 = Arduino Nano (Rev3.0)
  LED2 = LED - 5mm [color="Blue (470nm)" package="5 mm [THT]"]
  LED3 = LED - 5mm [color="Green (555nm)" package="5 mm [THT]"]
  R1 = Rotary Potentiometer (Small) [maximum_resistance=100kΩ package=THT]

nets:
  VCC: DS1.VDD, BMP280_Breakout1.VCC, Componente2.VCC, MQ-3_Sensor1.5V, Componente3.5V, R1.leg1, R1.leg2
  N1: DS1.DQ, Componente3.D2
  GND: DS1.GND, BMP280_Breakout1.GND, LED1.cathode, Componente2.GND, MQ-3_Sensor1.GND, Componente3.GND, LED2.cathode, LED3.cathode
  N2: BMP280_Breakout1.SCL, Componente3.A5
  N3: BMP280_Breakout1.SDA, Componente3.A4
  N4: LED1.anode, Componente3.A3
  N5: Componente1.POS, Componente2.POS
  N6: Componente1.NEG, Componente2.NEG
  N7: Componente2.AO, Componente3.A7
  N8: MQ-3_Sensor1.AOUT, Componente3.A0
  N9: Componente3.A6, LED3.anode
  N10: Componente3.A2, LED2.anode
  N11: Componente3.A1, R1.wiper

notes:
  pHmetro
  v1.3 BIOT
  mQ135 A0
  pH A1
  led Azul A2
  led Rojo A3
  bme280 - SDA A4
  bme280 - SCL A5
  led Verde A6
  Conductividad A7
  ds18x20 D2
  mq135

custom parts:
  BMP280 Breakout Board: This is a breakout board for the Bosch Sensortec BMP280, "an absolute barometric pressure sensor especially designed for mobile applications." The operation range is 300 to 1100 hPa. Supply voltage is 1.2 to 3.6V. Operating temperature range is -40 to +85 °C.
  FC-28 Soil Hygrometer Module - Probe: The FC-28 is a soil hygrometer module that uses the Texas Instruments LM393 comparator chip to provide an analog measurement of soil humidity.
  FC-28 Soil Hygrometer Module: The FC-28 is a soil hygrometer module that uses the Texas Instruments LM393 comparator chip to provide an analog measurement of soil humidity. The digital output is high when soil moisture is over a certain threshold, as determined by adjusting the potentiometer.
  MQ-3 Breakout Board: MQ-3 alcohol gas sensor breakout board. Input voltage is 5V. Sensor output is available in analog and digital.
